# Fritzing sketch sketch-flash (saved by Fritzing 0.9.6b)
breadboards: 1

parts:
  U1 = ESP8266 ESP-01 Upgraded WiFi Module [part_number=ESP8266]
  Part1 = FTDI Basic Programmer
  R2 = Resistor [tolerance=±5% power=0.25 resistance=10k package=THT]
  S1 = Pushbutton [package="[THT]"]
  R3 = Resistor [tolerance=±5% power=0.25 resistance=220 package=THT]

nets:
  N1: U1.RXD, Part1.TXO
  N2: U1.VCC, Part1.POWER, R3.Pin_1
  GND: U1.GPIO_0, U1.GND, Part1.GND, R2.Pin_1, S1.Pin_3, S1.Pin_4
  N3: U1.RST/GPIO_16, S1.Pin_1, S1.Pin_2, R3.Pin_0
  N4: U1.CH_PD, R2.Pin_0
  N5: U1.TXD, Part1.RXI

custom parts:
  ESP8266 ESP-01 Upgraded WiFi Module: Upgraded Version ESP-01,all Flash are upgraded to 1M byte.Also support Cloud service remote transmission.
  FTDI Basic Programmer: Description: This is the newest revision of our FTDI Basic. We now use a SMD 6-pin header on the bottom, which makes it smaller and more compact. Functionality has remained the same. This is a basic breakout board for the FTDI FT232RL USB to serial IC. The pinout of this board matches the FTDI cable to work with official Arduino and cloned 3.3V Arduino boards. It can also be used for general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
