# Fritzing sketch sketch (saved by Fritzing 0.9.6b)
breadboards: 1

parts:
  U1 = ESP8266 ESP-01 Upgraded WiFi Module [part_number=ESP8266]
  GY1 = GY-521 (MPU-6050) [form="♀ (female)" package=THT]
  Part1 = FTDI Basic Programmer

nets:
  N1: U1.RXD, Part1.TXO
  N2: U1.VCC, GY1.pin1, Part1.POWER
  N3: U1.GPIO_0, GY1.pin4
  N4: U1.GPIO_2, GY1.pin3
  GND: U1.GND, GY1.pin2, Part1.GND
  N5: U1.TXD, Part1.RXI

custom parts:
  ESP8266 ESP-01 Upgraded WiFi Module: Upgraded Version ESP-01,all Flash are upgraded to 1M byte.Also support Cloud service remote transmission.
  GY-521 (MPU-6050): Placa GY-521 basada en conjunto de acelerómetro+giroscopios MPU-6050
  FTDI Basic Programmer: Description: This is the newest revision of our FTDI Basic. We now use a SMD 6-pin header on the bottom, which makes it smaller and more compact. Functionality has remained the same. This is a basic breakout board for the FTDI FT232RL USB to serial IC. The pinout of this board matches the FTDI cable to work with official Arduino and cloned 3.3V Arduino boards. It can also be used for general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
